# Fritzing sketch LED-with-battery (saved by Fritzing 0.9.2b)
circuit board: 8.46667cm x 5.64444cm
breadboards: 1

parts:
  R1 = Resistor [tolerance=±5% resistance=220 package=THT]
  LED1 = LED - 5mm [color="Red (633nm)" package="5 mm [THT]"]
  VCC1 = Battery

nets:
  N1: R1.Pin_0, LED1.anode
  N2: R1.Pin_1, VCC1.+
  N3: LED1.cathode, VCC1.-
