# Fritzing sketch LED-with-nano (saved by Fritzing 0.9.2b)
circuit board: 8.46667cm x 5.64444cm
breadboards: 1

parts:
  R1 = Resistor [tolerance=±5% resistance=220 package=THT]
  LED1 = LED - 5mm [color="Red (633nm)" package="5 mm [THT]"]
  Part1 = Arduino Nano (Rev3.0)

nets:
  N1: R1.Pin_0, LED1.anode
  N2: R1.Pin_1, Part1.D13/SCK
  N3: LED1.cathode, Part1.GND
