# Fritzing sketch LEDs-with-nano (saved by Fritzing 0.9.2b)
circuit board: 5.14312cm x 4.83229cm
breadboards: 1

parts:
  LED1 = LED - 5mm [color="Red (633nm)" package="5 mm [THT]"]
  LED2 = LED - 5mm [color="Red (633nm)" package="5 mm [THT]"]
  LED3 = LED - 5mm [color="Red (633nm)" package="5 mm [THT]"]
  LED4 = LED - 5mm [color="Red (633nm)" package="5 mm [THT]"]
  LED5 = LED - 5mm [color="Red (633nm)" package="5 mm [THT]"]
  R1 = Resistor [tolerance=±5% resistance=330 package=THT]
  R2 = Resistor [tolerance=±5% resistance=330 package=THT]
  R3 = Resistor [tolerance=±5% resistance=330 package=THT]
  R4 = Resistor [tolerance=±5% resistance=330 package=THT]
  R5 = Resistor [tolerance=±5% resistance=330 package=THT]
  Part1 = Arduino Nano (Rev3.0)

nets:
  GND: LED1.cathode, LED2.cathode, LED3.cathode, LED4.cathode, LED5.cathode, Part1.GND
  N1: LED1.anode, R1.Pin_1
  N2: LED2.anode, R2.Pin_1
  N3: LED3.anode, R3.Pin_1
  N4: LED4.anode, R4.Pin_1
  N5: LED5.anode, R5.Pin_1
  N6: R1.Pin_0, Part1.D6
  N7: R2.Pin_0, Part1.D5
  N8: R3.Pin_0, Part1.D4
  N9: R4.Pin_0, Part1.D3
  N10: R5.Pin_0, Part1.D2
