# Fritzing sketch lampboard-8 (saved by Fritzing 0.9.2b)
circuit board: 9.68718cm x 5.60204cm
breadboards: 1

parts:
  Q1 = NPN-Transistor [package="TO92 [THT]"]
  Q2 = NPN-Transistor [package="TO92 [THT]"]
  Q3 = NPN-Transistor [package="TO92 [THT]"]
  Q4 = NPN-Transistor [package="TO92 [THT]"]
  Q5 = NPN-Transistor [package="TO92 [THT]"]
  Q6 = NPN-Transistor [package="TO92 [THT]"]
  R1 = Resistor [tolerance=±5% resistance=220 package=THT]
  R2 = Resistor [tolerance=±5% resistance=220 package=THT]
  R3 = Resistor [tolerance=±5% resistance=220 package=THT]
  R4 = Resistor [tolerance=±5% resistance=220 package=THT]
  R5 = Resistor [tolerance=±5% resistance=220 package=THT]
  R6 = Resistor [tolerance=±5% resistance=220 package=THT]
  LED1 = LED - 5mm [color="Red (633nm)" package="5 mm [THT]"]
  LED2 = LED - 5mm [color="Red (633nm)" package="5 mm [THT]"]
  LED3 = LED - 5mm [color="Red (633nm)" package="5 mm [THT]"]
  LED4 = LED - 5mm [color="Red (633nm)" package="5 mm [THT]"]
  LED5 = LED - 5mm [color="Red (633nm)" package="5 mm [THT]"]
  LED6 = LED - 5mm [color="Red (633nm)" package="5 mm [THT]"]
  Q7 = NPN-Transistor [package="TO92 [THT]"]
  Q8 = NPN-Transistor [package="TO92 [THT]"]
  R7 = Resistor [tolerance=±5% resistance=220 package=THT]
  R12 = Resistor [tolerance=±5% resistance=220 package=THT]
  LED8 = LED - 5mm [color="Red (633nm)" package="5 mm [THT]"]
  LED11 = LED - 5mm [color="Red (633nm)" package="5 mm [THT]"]
  R13 = Resistor [tolerance=±5% resistance=220 package=THT]
  R14 = Resistor [tolerance=±5% resistance=220 package=THT]
  R15 = Resistor [tolerance=±5% resistance=220 package=THT]
  R16 = Resistor [tolerance=±5% resistance=220 package=THT]
  R17 = Resistor [tolerance=±5% resistance=220 package=THT]
  R18 = Resistor [tolerance=±5% resistance=220 package=THT]
  R19 = Resistor [tolerance=±5% resistance=220 package=THT]
  R20 = Resistor [tolerance=±5% resistance=220 package=THT]
  JP1 = Header 12 [package=1x12_machine-pin-header_lock.004]
  Q9 = NPN-Transistor [package="TO92 [THT]"]
  LED12 = LED - 5mm [color="Red (633nm)" package="5 mm [THT]"]
  R21 = Resistor [tolerance=±5% resistance=220 package=THT]
  R22 = Resistor [tolerance=±5% resistance=220 package=THT]

nets:
  N1: Q1.E, Q2.E, Q3.E, Q4.E, Q5.E, Q6.E, Q7.E, Q8.E, JP1.11, Q9.E
  N2: Q1.B, R14.Pin_1
  N3: Q1.C, LED2.cathode
  N4: Q2.B, R13.Pin_1
  N5: Q2.C, LED1.cathode
  N6: Q3.B, R15.Pin_1
  N7: Q3.C, LED3.cathode
  N8: Q4.B, R16.Pin_1
  N9: Q4.C, LED4.cathode
  N10: Q5.B, R18.Pin_1
  N11: Q5.C, LED6.cathode
  N12: Q6.B, R17.Pin_1
  N13: Q6.C, LED5.cathode
  N14: R1.Pin_0, LED1.anode
  N15: R1.Pin_1, R2.Pin_1, R3.Pin_1, R4.Pin_1, R5.Pin_1, R6.Pin_1, R7.Pin_1, R12.Pin_1, JP1.12
  N16: R2.Pin_0, LED2.anode
  N17: R3.Pin_0, LED3.anode
  N18: R4.Pin_0, LED4.anode
  N19: R5.Pin_0, LED5.anode
  N20: R6.Pin_0, LED6.anode
  N21: Q7.B, R20.Pin_1
  N22: Q7.C, LED11.cathode
  N23: Q8.B, R19.Pin_1
  N24: Q8.C, LED8.cathode
  N25: R7.Pin_0, LED8.anode
  N26: R12.Pin_0, LED11.anode
  N27: R13.Pin_0, JP1.9
  N28: R14.Pin_0, JP1.8
  N29: R15.Pin_0, JP1.7
  N30: R16.Pin_0, JP1.6
  N31: R17.Pin_0, JP1.5
  N32: R18.Pin_0, JP1.4
  N33: R19.Pin_0, JP1.3
  N34: R20.Pin_0, JP1.2
  N35: JP1.10, R22.Pin_1
  N36: Q9.B, R22.Pin_0
  N37: Q9.C, LED12.cathode
  N38: LED12.anode, R21.Pin_1
