# Fritzing sketch 9leds (saved by Fritzing 0.9.2b)
circuit board: 9.46787cm x 5.67359cm
breadboards: 1

parts:
  Q1 = NPN-Transistor [package="TO92 [THT]"]
  Q2 = NPN-Transistor [package="TO92 [THT]"]
  Q3 = NPN-Transistor [package="TO92 [THT]"]
  Q4 = NPN-Transistor [package="TO92 [THT]"]
  Q5 = NPN-Transistor [package="TO92 [THT]"]
  Q6 = NPN-Transistor [package="TO92 [THT]"]
  Q7 = NPN-Transistor [package="TO92 [THT]"]
  Q8 = NPN-Transistor [package="TO92 [THT]"]
  Q9 = NPN-Transistor [package="TO92 [THT]"]
  R1 = Resistor [tolerance=±5% resistance=220 package=THT]
  R2 = Resistor [tolerance=±5% resistance=220 package=THT]
  R3 = Resistor [tolerance=±5% resistance=220 package=THT]
  R4 = Resistor [tolerance=±5% resistance=220 package=THT]
  R5 = Resistor [tolerance=±5% resistance=220 package=THT]
  R6 = Resistor [tolerance=±5% resistance=220 package=THT]
  R7 = Resistor [tolerance=±5% resistance=220 package=THT]
  R8 = Resistor [tolerance=±5% resistance=220 package=THT]
  R9 = Resistor [tolerance=±5% resistance=220 package=THT]
  LED1 = LED - 5mm [color="Red (633nm)" package="5 mm [THT]"]
  LED2 = LED - 5mm [color="Red (633nm)" package="5 mm [THT]"]
  LED3 = LED - 5mm [color="Red (633nm)" package="5 mm [THT]"]
  LED4 = LED - 5mm [color="Red (633nm)" package="5 mm [THT]"]
  LED5 = LED - 5mm [color="Red (633nm)" package="5 mm [THT]"]
  LED6 = LED - 5mm [color="Red (633nm)" package="5 mm [THT]"]
  LED7 = LED - 5mm [color="Red (633nm)" package="5 mm [THT]"]
  LED8 = LED - 5mm [color="Red (633nm)" package="5 mm [THT]"]
  LED9 = LED - 5mm [color="Red (633nm)" package="5 mm [THT]"]
  R10 = Resistor [tolerance=±5% resistance=220 package=THT]
  R11 = Resistor [tolerance=±5% resistance=220 package=THT]
  R12 = Resistor [tolerance=±5% resistance=220 package=THT]
  R13 = Resistor [tolerance=±5% resistance=220 package=THT]
  R14 = Resistor [tolerance=±5% resistance=220 package=THT]
  R15 = Resistor [tolerance=±5% resistance=220 package=THT]
  R16 = Resistor [tolerance=±5% resistance=220 package=THT]
  R17 = Resistor [tolerance=±5% resistance=220 package=THT]
  R18 = Resistor [tolerance=±5% resistance=220 package=THT]
  J1 = female pin header, 11 pins [form="♀ (female)"]

nets:
  N1: Q1.E, Q2.E, Q3.E, Q4.E, Q5.E, Q6.E, Q7.E, Q8.E, Q9.E
  N2: Q1.B, R10.Pin_0
  N3: Q1.C, R1.Pin_1
  N4: Q2.B, R11.Pin_0
  N5: Q2.C, R2.Pin_1
  N6: Q3.B, R12.Pin_0
  N7: Q3.C, R3.Pin_1
  N8: Q4.B, R13.Pin_0
  N9: Q4.C, R4.Pin_1
  N10: Q5.B, R14.Pin_0
  N11: Q5.C, R5.Pin_1
  N12: Q6.B, R15.Pin_0
  N13: Q6.C, R6.Pin_1
  N14: Q7.B, R16.Pin_0
  N15: Q7.C, R7.Pin_1
  N16: Q8.B, R17.Pin_0
  N17: Q8.C, R8.Pin_1
  N18: Q9.B, R18.Pin_0
  N19: Q9.C, R9.Pin_1
  N20: R1.Pin_0, LED1.cathode
  N21: R2.Pin_0, LED2.cathode
  N22: R3.Pin_0, LED3.cathode
  N23: R4.Pin_0, LED4.cathode
  N24: R5.Pin_0, LED5.cathode
  N25: R6.Pin_0, LED6.cathode
  N26: R7.Pin_0, LED7.cathode
  N27: R8.Pin_0, LED8.cathode
  N28: R9.Pin_0, LED9.cathode
  N29: LED1.anode, LED2.anode, LED3.anode, LED4.anode, LED5.anode, LED6.anode, LED7.anode, LED8.anode, LED9.anode
  N30: R10.Pin_1, J1.pin1
  N31: R11.Pin_1, J1.pin2
  N32: R12.Pin_1, J1.pin3
