# Fritzing sketch Engima-LCD (saved by Fritzing 0.9.2b)
breadboards: 1

parts:
  Part1 = Arduino Nano (Rev3.0)
  LCD1 = LCD screen
  R1 = Trimmer Potentiometer [maximum_resistance=10kΩ package=THT]

nets:
  GND: Part1.GND, LCD1.VSS, LCD1.R/W, R1.leg1
  N1: Part1.D7, LCD1.DB7
  N2: Part1.D8, LCD1.DB6
  N3: Part1.D9, LCD1.DB5
  N4: Part1.D10, LCD1.DB4
  N5: Part1.D11/MOSI, LCD1.E
  N6: Part1.D12/MISO, LCD1.RS
  5V: Part1.5V, LCD1.VDD, R1.leg2
  N7: LCD1.V0, R1.wiper
